// Logisim project stage2.circ as structural Verilog: 2 circuits, main circuit main
module main (
);

  wire button_1_out, total_1_out_2;
  wire [3:0] total_1_out_3;

  Clock clock_1 ();  // open: out
  Hex_Digit_Display hex_digit_display_1 ();  // open: value, dp
  Hex_Digit_Display hex_digit_display_2 ();  // open: value, dp
  Button button_1 (.out(button_1_out));
  Hex_Digit_Display hex_digit_display_3 ();  // open: value, dp
  Hex_Digit_Display hex_digit_display_4 (.value(total_1_out_3));  // open: dp
  Button button_2 ();  // open: out
  Button button_3 ();  // open: out
  Hex_Digit_Display hex_digit_display_5 ();  // open: value, dp
  Hex_Digit_Display hex_digit_display_6 ();  // open: value, dp
  LED led_1 (.in(total_1_out_2));
  Hex_Digit_Display hex_digit_display_7 ();  // open: value, dp
  Hex_Digit_Display hex_digit_display_8 ();  // open: value, dp
  total total_1 (.in_1(button_1_out), .out_2(total_1_out_2), .out_3(total_1_out_3));

  // Notes on the sheet:
  //   Elapsed Time
  //   Minutes
  //   :
  //   Start / Stop
  //   Seconds
  //   Stopwatch Interface
  //   Split
  //   Reset
  //   Minutes
  //   Clock Started
  //   Split Time
  //   :
  //   Seconds
endmodule

module total (
  input  in_1,
  output out_2,
  output [3:0] out_3
);

  wire and_1_out, and_2_out, clock_1_out, t_ff_2_q, t_ff_3_q, t_ff_4_q, t_ff_5_q;

  T_Flip_Flop t_ff_1 (.T(1'b1), .clk(in_1), .Q(out_2));  // open: Qn, reset, preset
  Clock clock_1 (.out(clock_1_out));
  and and_1 (and_1_out, clock_1_out, out_2);
  T_Flip_Flop #(.trigger("falling")) t_ff_2 (
    .T(1'b1), .clk(and_1_out), .Q(t_ff_2_q), .reset(and_2_out));  // open: Qn, preset
  T_Flip_Flop #(.trigger("falling")) t_ff_3 (
    .T(1'b1), .clk(t_ff_2_q), .Q(t_ff_3_q), .reset(and_2_out));  // open: Qn, preset
  D_Flip_Flop d_ff_1 (.D(t_ff_2_q), .clk(and_1_out), .Q(out_3[0]));  // open: Qn, preset, reset
  D_Flip_Flop d_ff_2 (.D(t_ff_3_q), .clk(and_1_out), .Q(out_3[1]));  // open: Qn, preset, reset
  T_Flip_Flop #(.trigger("falling")) t_ff_4 (
    .T(1'b1), .clk(t_ff_3_q), .Q(t_ff_4_q), .reset(and_2_out));  // open: Qn, preset
  D_Flip_Flop d_ff_3 (.D(t_ff_4_q), .clk(and_1_out), .Q(out_3[2]));  // open: Qn, preset, reset
  T_Flip_Flop #(.trigger("falling")) t_ff_5 (
    .T(1'b1), .clk(t_ff_4_q), .Q(t_ff_5_q), .reset(and_2_out));  // open: Qn, preset
  and and_2 (and_2_out, t_ff_3_q, t_ff_5_q);
  D_Flip_Flop d_ff_4 (.D(t_ff_5_q), .clk(and_1_out), .Q(out_3[3]));  // open: Qn, preset, reset
endmodule
