// Logisim project stage3.circ as structural Verilog: 2 circuits, main circuit main
module main (
);

  wire button_1_out, button_3_out, total_1_led;
  wire [3:0] total_1_first_second, total_1_second_second;

  Clock clock_1 ();  // open: out
  Hex_Digit_Display hex_digit_display_1 ();  // open: value, dp
  Hex_Digit_Display hex_digit_display_2 ();  // open: value, dp
  Button button_1 (.out(button_1_out));
  Hex_Digit_Display hex_digit_display_3 (.value(total_1_second_second));  // open: dp
  Hex_Digit_Display hex_digit_display_4 (.value(total_1_first_second));  // open: dp
  Button button_2 ();  // open: out
  Button button_3 (.out(button_3_out));
  Hex_Digit_Display hex_digit_display_5 ();  // open: value, dp
  Hex_Digit_Display hex_digit_display_6 ();  // open: value, dp
  LED led_1 (.in(total_1_led));
  Hex_Digit_Display hex_digit_display_7 ();  // open: value, dp
  Hex_Digit_Display hex_digit_display_8 ();  // open: value, dp
  total total_1 (
    .reset(button_3_out), .start(button_1_out), .LED(total_1_led), .first_second(total_1_first_second),
    .second_second(total_1_second_second));  // open: in_3

  // Notes on the sheet:
  //   Elapsed Time
  //   Minutes
  //   :
  //   Start / Stop
  //   Seconds
  //   Stopwatch Interface
  //   Split
  //   Reset
  //   Minutes
  //   Clock Started
  //   Split Time
  //   :
  //   Seconds
endmodule

module total (
  input  reset,
  input  start,
  input  in_3,
  output LED,
  output [3:0] first_second,
  output [3:0] second_second
);

  wire and_1_out, and_2_out, and_3_out, and_4_out, and_5_out, and_6_out, clock_1_out, clock_2_out, or_1_out,
       or_2_out, or_3_out, t_ff_2_q, t_ff_3_q, t_ff_4_q, t_ff_5_q, t_ff_6_q, t_ff_7_q, t_ff_8_q;

  and and_1 (and_1_out, and_5_out, LED);
  T_Flip_Flop t_ff_1 (.T(1'b1), .clk(or_1_out), .Q(LED));  // open: Qn, reset, preset
  or or_1 (or_1_out, start, and_1_out);
  Clock clock_1 (.out(clock_1_out));
  and and_2 (and_2_out, clock_1_out, LED);
  and and_3 (and_3_out, first_second[0], first_second[3]);
  T_Flip_Flop #(.trigger("falling")) t_ff_2 (
    .T(1'b1), .clk(and_2_out), .Q(t_ff_2_q), .reset(or_2_out));  // open: Qn, preset
  T_Flip_Flop #(.trigger("falling")) t_ff_3 (
    .T(1'b1), .clk(t_ff_2_q), .Q(t_ff_3_q), .reset(or_2_out));  // open: Qn, preset
  D_Flip_Flop d_ff_1 (.D(t_ff_2_q), .clk(and_2_out), .Q(first_second[0]), .reset(and_5_out));  // open: Qn, preset
  D_Flip_Flop d_ff_2 (.D(t_ff_3_q), .clk(and_2_out), .Q(first_second[1]), .reset(and_5_out));  // open: Qn, preset
  Clock clock_2 (.out(clock_2_out));
  T_Flip_Flop #(.trigger("falling")) t_ff_4 (
    .T(1'b1), .clk(t_ff_3_q), .Q(t_ff_4_q), .reset(or_2_out));  // open: Qn, preset
  T_Flip_Flop #(.trigger("falling")) t_ff_5 (
    .T(and_3_out), .clk(clock_2_out), .Q(t_ff_5_q), .reset(or_3_out));  // open: Qn, preset
  D_Flip_Flop d_ff_3 (.D(t_ff_4_q), .clk(and_2_out), .Q(first_second[2]), .reset(and_5_out));  // open: Qn, preset
  T_Flip_Flop #(.trigger("falling")) t_ff_6 (
    .T(and_3_out), .clk(t_ff_5_q), .Q(t_ff_6_q), .reset(or_3_out));  // open: Qn, preset
  D_Flip_Flop d_ff_4 (.D(t_ff_5_q), .clk(clock_2_out), .Q(second_second[0]), .reset(and_5_out));  // open: Qn, preset
  T_Flip_Flop #(.trigger("falling")) t_ff_7 (
    .T(1'b1), .clk(t_ff_4_q), .Q(t_ff_7_q), .reset(or_2_out));  // open: Qn, preset
  D_Flip_Flop d_ff_5 (.D(t_ff_6_q), .clk(clock_2_out), .Q(second_second[1]), .reset(and_5_out));  // open: Qn, preset
  and and_4 (and_4_out, t_ff_3_q, t_ff_7_q);
  or or_2 (or_2_out, and_4_out, and_5_out);
  D_Flip_Flop d_ff_6 (.D(t_ff_7_q), .clk(and_2_out), .Q(first_second[3]), .reset(and_5_out));  // open: Qn, preset
  T_Flip_Flop #(.trigger("falling")) t_ff_8 (
    .T(and_3_out), .clk(t_ff_6_q), .Q(t_ff_8_q), .reset(or_3_out));  // open: Qn, preset
  and and_5 (and_5_out, LED, reset);
  D_Flip_Flop d_ff_7 (.D(t_ff_8_q), .clk(clock_2_out), .Q(second_second[2]), .reset(and_5_out));  // open: Qn, preset
  and and_6 (and_6_out, t_ff_8_q, t_ff_6_q);
  or or_3 (or_3_out, and_6_out, and_5_out);

  assign second_second[3] = in_3;
endmodule
