// Logisim project stage6.circ as structural Verilog: 9 circuits, main circuit main
module main (
);

  wire button_1_out, button_2_out, button_3_out, total_1_led;
  wire [3:0] total_1_data_first_min, total_1_data_first_min_2, total_1_data_first_min_3,
       total_1_data_first_min_4, total_1_data_first_min_5, total_1_data_first_sec, total_1_data_first_sec_2,
       total_1_data_first_sec_3, total_1_data_first_sec_4, total_1_data_first_sec_5, total_1_data_second_min,
       total_1_data_second_min_2, total_1_data_second_min_3, total_1_data_second_min_4,
       total_1_data_second_min_5, total_1_data_second_sec, total_1_data_second_sec_2,
       total_1_data_second_sec_3, total_1_data_second_sec_4, total_1_data_second_sec_5,
       total_1_first_min_col, total_1_first_sec_col, total_1_second_min_col, total_1_second_sec_col;

  Clock clock_1 ();  // open: out
  Hex_Digit_Display hex_digit_display_1 (.value(total_1_second_min_col));  // open: dp
  Hex_Digit_Display hex_digit_display_2 (.value(total_1_first_min_col));  // open: dp
  Button button_1 (.out(button_1_out));
  Hex_Digit_Display hex_digit_display_3 (.value(total_1_second_sec_col));  // open: dp
  Hex_Digit_Display hex_digit_display_4 (.value(total_1_first_sec_col));  // open: dp
  Button button_2 (.out(button_2_out));
  Button button_3 (.out(button_3_out));
  Hex_Digit_Display hex_digit_display_5 (.value(total_1_data_second_min));  // open: dp
  Hex_Digit_Display hex_digit_display_6 (.value(total_1_data_first_min));  // open: dp
  LED led_1 (.in(total_1_led));
  Hex_Digit_Display hex_digit_display_7 (.value(total_1_data_second_sec));  // open: dp
  Hex_Digit_Display hex_digit_display_8 (.value(total_1_data_first_sec));  // open: dp
  total total_1 (
    .reset(button_3_out), .split(button_2_out), .on_off(button_1_out), .LED(total_1_led),
    .first_sec_col(total_1_first_sec_col),
    .data_first_sec({total_1_data_first_sec_5, total_1_data_first_sec_4, total_1_data_first_sec_3, total_1_data_first_sec_2, total_1_data_first_sec}),
    .second_sec_col(total_1_second_sec_col),
    .data_second_sec({total_1_data_second_sec_5, total_1_data_second_sec_4, total_1_data_second_sec_3, total_1_data_second_sec_2, total_1_data_second_sec}),
    .first_min_col(total_1_first_min_col),
    .data_first_min({total_1_data_first_min_5, total_1_data_first_min_4, total_1_data_first_min_3, total_1_data_first_min_2, total_1_data_first_min}),
    .second_min_col(total_1_second_min_col),
    .data_second_min({total_1_data_second_min_5, total_1_data_second_min_4, total_1_data_second_min_3, total_1_data_second_min_2, total_1_data_second_min}));
  Hex_Digit_Display hex_digit_display_9 (.value(total_1_data_second_min_2));  // open: dp
  Hex_Digit_Display hex_digit_display_10 (.value(total_1_data_first_min_2));  // open: dp
  Hex_Digit_Display hex_digit_display_11 (.value(total_1_data_second_sec_2));  // open: dp
  Hex_Digit_Display hex_digit_display_12 (.value(total_1_data_first_sec_2));  // open: dp
  Hex_Digit_Display hex_digit_display_13 (.value(total_1_data_second_min_3));  // open: dp
  Hex_Digit_Display hex_digit_display_14 (.value(total_1_data_first_min_3));  // open: dp
  Hex_Digit_Display hex_digit_display_15 (.value(total_1_data_second_sec_3));  // open: dp
  Hex_Digit_Display hex_digit_display_16 (.value(total_1_data_first_sec_3));  // open: dp
  Hex_Digit_Display hex_digit_display_17 (.value(total_1_data_second_min_4));  // open: dp
  Hex_Digit_Display hex_digit_display_18 (.value(total_1_data_first_min_4));  // open: dp
  Hex_Digit_Display hex_digit_display_19 (.value(total_1_data_second_sec_4));  // open: dp
  Hex_Digit_Display hex_digit_display_20 (.value(total_1_data_first_sec_4));  // open: dp
  Hex_Digit_Display hex_digit_display_21 (.value(total_1_data_second_min_5));  // open: dp
  Hex_Digit_Display hex_digit_display_22 (.value(total_1_data_first_min_5));  // open: dp
  Hex_Digit_Display hex_digit_display_23 (.value(total_1_data_second_sec_5));  // open: dp
  Hex_Digit_Display hex_digit_display_24 (.value(total_1_data_first_sec_5));  // open: dp

  // Notes on the sheet:
  //   Elapsed Time
  //   Minutes
  //   :
  //   Start / Stop
  //   Seconds
  //   Stopwatch Interface
  //   Split
  //   Reset
  //   Minutes
  //   Clock Started
  //   Split Time
  //   :
  //   Seconds
  //   Minutes
  //   Seconds
  //   :
  //   Minutes
  //   :
  //   Seconds
  //   Minutes
  //   Seconds
  //   :
  //   Minutes
  //   :
  //   Seconds
endmodule

module total (
  input  reset,
  input  split,
  input  on_off,
  output LED,
  output [3:0] first_sec_col,
  output [19:0] data_first_sec,
  output [3:0] second_sec_col,
  output [19:0] data_second_sec,
  output [3:0] first_min_col,
  output [19:0] data_first_min,
  output [3:0] second_min_col,
  output [19:0] data_second_min
);

  wire and_1_out, and_2_out, and_3_out, and_4_out, clock_1_out, prevent_illegal_five_1_run_next_col_con_1,
       prevent_illegal_five_1_run_next_col_con_2, prevent_illegal_nine_1_run_next_col_con_1,
       prevent_illegal_nine_1_run_next_col_con_2, prevent_illegal_nine_2_run_next_col_con_1,
       prevent_illegal_nine_2_run_next_col_con_2, ripple_counter_five_1_out1, ripple_counter_five_1_out2,
       ripple_counter_five_1_out3, ripple_counter_nine_1_out1, ripple_counter_nine_1_out2,
       ripple_counter_nine_1_out3, ripple_counter_nine_1_out4, ripple_counter_nine_2_out1,
       ripple_counter_nine_2_out2, ripple_counter_nine_2_out3, ripple_counter_nine_2_out4,
       ripple_counter_nine_3_out1, ripple_counter_nine_3_out2, ripple_counter_nine_3_out3,
       ripple_counter_nine_3_out4, start_stop_1_run, start_stop_1_split_con;

  start_stop start_stop_1 (
    .on_off(on_off), .reset(reset), .split_con(start_stop_1_split_con), .LED(LED), .run(start_stop_1_run));
  Clock clock_1 (.out(clock_1_out));
  ripple_counter_nine ripple_counter_nine_1 (
    .inp(start_stop_1_run), .reset(reset), .clock(clock_1_out), .out1(ripple_counter_nine_1_out1),
    .out2(ripple_counter_nine_1_out2), .out3(ripple_counter_nine_1_out3), .out4(ripple_counter_nine_1_out4));
  ripple_counter_five ripple_counter_five_1 (
    .inp(and_1_out), .reset(reset), .clock(clock_1_out), .out1(ripple_counter_five_1_out1),
    .out2(ripple_counter_five_1_out2), .out3(ripple_counter_five_1_out3));
  ripple_counter_nine ripple_counter_nine_2 (
    .inp(and_2_out), .reset(reset), .clock(clock_1_out), .out1(ripple_counter_nine_2_out1),
    .out2(ripple_counter_nine_2_out2), .out3(ripple_counter_nine_2_out3), .out4(ripple_counter_nine_2_out4));
  ripple_counter_nine ripple_counter_nine_3 (
    .inp(and_3_out), .reset(reset), .clock(clock_1_out), .out1(ripple_counter_nine_3_out1),
    .out2(ripple_counter_nine_3_out2), .out3(ripple_counter_nine_3_out3), .out4(ripple_counter_nine_3_out4));
  prevent_illegal_nine prevent_illegal_nine_1 (
    .inp1(ripple_counter_nine_1_out1), .inp2(ripple_counter_nine_1_out2), .inp3(ripple_counter_nine_1_out3),
    .inp4(ripple_counter_nine_1_out4), .reset(reset), .clock(clock_1_out), .outp(first_sec_col),
    .run_next_col_con_2(prevent_illegal_nine_1_run_next_col_con_2),
    .run_next_col_con_1(prevent_illegal_nine_1_run_next_col_con_1));
  prevent_illegal_five prevent_illegal_five_1 (
    .inp1(ripple_counter_five_1_out1), .inp2(ripple_counter_five_1_out2), .inp3(ripple_counter_five_1_out3),
    .reset(reset), .clock(clock_1_out), .outp(second_sec_col),
    .run_next_col_con_1(prevent_illegal_five_1_run_next_col_con_1),
    .run_next_col_con_2(prevent_illegal_five_1_run_next_col_con_2));  // open: in_4
  prevent_illegal_nine prevent_illegal_nine_2 (
    .inp1(ripple_counter_nine_2_out1), .inp2(ripple_counter_nine_2_out2), .inp3(ripple_counter_nine_2_out3),
    .inp4(ripple_counter_nine_2_out4), .reset(reset), .clock(clock_1_out), .outp(first_min_col),
    .run_next_col_con_2(prevent_illegal_nine_2_run_next_col_con_2),
    .run_next_col_con_1(prevent_illegal_nine_2_run_next_col_con_1));
  prevent_illegal_nine prevent_illegal_nine_3 (
    .inp1(ripple_counter_nine_3_out1), .inp2(ripple_counter_nine_3_out2), .inp3(ripple_counter_nine_3_out3),
    .inp4(ripple_counter_nine_3_out4), .reset(reset), .clock(clock_1_out), .outp(second_min_col));  // open: run_next_col_con_2, run_next_col_con_1
  and and_1 (and_1_out, prevent_illegal_nine_1_run_next_col_con_2, prevent_illegal_nine_1_run_next_col_con_1);
  and and_2 (and_2_out, and_1_out, prevent_illegal_five_1_run_next_col_con_1, prevent_illegal_five_1_run_next_col_con_2);
  and and_3 (and_3_out, and_2_out, prevent_illegal_nine_2_run_next_col_con_2, prevent_illegal_nine_2_run_next_col_con_1);
  and and_4 (and_4_out, start_stop_1_split_con, split);
  split_5_times_circuit split_5_times_circuit_1 (
    .reset(reset), .split(and_4_out), .inpt(first_sec_col), .stored_data1(data_first_sec[3:0]),
    .stored_data2(data_first_sec[7:4]), .stored_data3(data_first_sec[11:8]),
    .stored_data4(data_first_sec[15:12]), .stored_data5(data_first_sec[19:16]));
  split_5_times_circuit split_5_times_circuit_2 (
    .reset(reset), .split(and_4_out), .inpt(second_sec_col), .stored_data1(data_second_sec[3:0]),
    .stored_data2(data_second_sec[7:4]), .stored_data3(data_second_sec[11:8]),
    .stored_data4(data_second_sec[15:12]), .stored_data5(data_second_sec[19:16]));
  split_5_times_circuit split_5_times_circuit_3 (
    .reset(reset), .split(and_4_out), .inpt(first_min_col), .stored_data1(data_first_min[3:0]),
    .stored_data2(data_first_min[7:4]), .stored_data3(data_first_min[11:8]),
    .stored_data4(data_first_min[15:12]), .stored_data5(data_first_min[19:16]));
  split_5_times_circuit split_5_times_circuit_4 (
    .reset(reset), .split(and_4_out), .inpt(second_min_col), .stored_data1(data_second_min[3:0]),
    .stored_data2(data_second_min[7:4]), .stored_data3(data_second_min[11:8]),
    .stored_data4(data_second_min[15:12]), .stored_data5(data_second_min[19:16]));

  // Notes on the sheet:
  //   START_STOP
  //   FIRST COLUMN OF SECONDS
  //   SECOND COLUMN OF SECONDS
  //   RESET
  //   FIRST COLUMN OF MINUTES
  //   SECOND COLUMN OF MINUTES
  //   SPLIT
  //   SPLITTED DATA OF COLUMN
  //   SPLITTED DATA OF COLUMN
  //   SPLITTED DATA OF COLUMN
  //   SPLITTED DATA OF COLUMN
endmodule

module start_stop (
  input  on_off,
  input  reset,
  output split_con,
  output LED,
  output run
);

  wire and_1_out, or_1_out;

  and and_1 (and_1_out, reset, LED);
  T_Flip_Flop t_ff_1 (.T(1'b1), .clk(or_1_out), .Q(LED));  // open: Qn, reset, preset
  or or_1 (or_1_out, on_off, and_1_out);

  assign run = LED;
  assign split_con = LED;
endmodule

module ripple_counter_nine (
  input  inp,
  input  reset,
  input  clock,
  output out1,
  output out2,
  output out3,
  output out4
);

  wire and_1_out, or_1_out;

  T_Flip_Flop #(.trigger("falling")) t_ff_1 (.T(inp), .clk(clock), .Q(out1), .reset(or_1_out));  // open: Qn, preset
  T_Flip_Flop #(.trigger("falling")) t_ff_2 (.T(inp), .clk(out1), .Q(out2), .reset(or_1_out));  // open: Qn, preset
  T_Flip_Flop #(.trigger("falling")) t_ff_3 (.T(inp), .clk(out2), .Q(out3), .reset(or_1_out));  // open: Qn, preset
  T_Flip_Flop #(.trigger("falling")) t_ff_4 (.T(inp), .clk(out3), .Q(out4), .reset(or_1_out));  // open: Qn, preset
  and and_1 (and_1_out, out2, out4);
  or or_1 (or_1_out, and_1_out, reset);
endmodule

module prevent_illegal_nine (
  input  inp1,
  input  inp2,
  input  inp3,
  input  inp4,
  input  reset,
  input  clock,
  output [3:0] outp,
  output run_next_col_con_2,
  output run_next_col_con_1
);

  D_Flip_Flop d_ff_1 (.D(inp1), .clk(clock), .Q(outp[0]), .reset(reset));  // open: Qn, preset
  D_Flip_Flop d_ff_2 (.D(inp2), .clk(clock), .Q(outp[1]), .reset(reset));  // open: Qn, preset
  D_Flip_Flop d_ff_3 (.D(inp3), .clk(clock), .Q(outp[2]), .reset(reset));  // open: Qn, preset
  D_Flip_Flop d_ff_4 (.D(inp4), .clk(clock), .Q(outp[3]), .reset(reset));  // open: Qn, preset

  assign run_next_col_con_1 = outp[3];
  assign run_next_col_con_2 = outp[0];
endmodule

module ripple_counter_five (
  input  inp,
  input  reset,
  input  clock,
  output out1,
  output out2,
  output out3
);

  wire and_1_out, or_1_out;

  T_Flip_Flop #(.trigger("falling")) t_ff_1 (.T(inp), .clk(clock), .Q(out1), .reset(or_1_out));  // open: Qn, preset
  T_Flip_Flop #(.trigger("falling")) t_ff_2 (.T(inp), .clk(out1), .Q(out2), .reset(or_1_out));  // open: Qn, preset
  T_Flip_Flop #(.trigger("falling")) t_ff_3 (.T(inp), .clk(out2), .Q(out3), .reset(or_1_out));  // open: Qn, preset
  and and_1 (and_1_out, out3, out2);
  or or_1 (or_1_out, and_1_out, reset);
endmodule

module prevent_illegal_five (
  input  inp1,
  input  inp2,
  input  inp3,
  input  in_4,
  input  reset,
  input  clock,
  output [3:0] outp,
  output run_next_col_con_1,
  output run_next_col_con_2
);

  D_Flip_Flop d_ff_1 (.D(inp1), .clk(clock), .Q(outp[0]), .reset(reset));  // open: Qn, preset
  D_Flip_Flop d_ff_2 (.D(inp2), .clk(clock), .Q(outp[1]), .reset(reset));  // open: Qn, preset
  D_Flip_Flop d_ff_3 (.D(inp3), .clk(clock), .Q(outp[2]), .reset(reset));  // open: Qn, preset

  assign outp[3] = in_4;
  assign run_next_col_con_1 = outp[0];
  assign run_next_col_con_2 = outp[2];
endmodule

module split_circuit (
  input  [3:0] inp,
  input  split,
  input  reset,
  output [3:0] outp
);

  D_Flip_Flop d_ff_1 (.D(inp[3]), .clk(split), .Q(outp[3]), .reset(reset));  // open: Qn, preset
  D_Flip_Flop d_ff_2 (.D(inp[2]), .clk(split), .Q(outp[2]), .reset(reset));  // open: Qn, preset
  D_Flip_Flop d_ff_3 (.D(inp[1]), .clk(split), .Q(outp[1]), .reset(reset));  // open: Qn, preset
  D_Flip_Flop d_ff_4 (.D(inp[0]), .clk(split), .Q(outp[0]), .reset(reset));  // open: Qn, preset
endmodule

module split_5_times_circuit (
  input  reset,
  input  split,
  input  [3:0] inpt,
  output [3:0] stored_data1,
  output [3:0] stored_data2,
  output [3:0] stored_data3,
  output [3:0] stored_data4,
  output [3:0] stored_data5
);

  split_circuit split_circuit_1 (.inp(inpt), .split(split), .reset(reset), .outp(stored_data1));
  split_circuit split_circuit_2 (.inp(stored_data1), .split(split), .reset(reset), .outp(stored_data2));
  split_circuit split_circuit_3 (.inp(stored_data2), .split(split), .reset(reset), .outp(stored_data3));
  split_circuit split_circuit_4 (.inp(stored_data3), .split(split), .reset(reset), .outp(stored_data4));
  split_circuit split_circuit_5 (.inp(stored_data4), .split(split), .reset(reset), .outp(stored_data5));
endmodule
